# Fritzing sketch Epar PCB (saved by Fritzing 0.9.3b)
circuit board: 8.22818cm x 8.38713cm

parts:
  LCD1 = LCD screen
  R1 = Resistor [tolerance=±5% resistance=47k package=THT]
  Q1 = NPN-Transistor [part_number=BFR96 package="TO92 [THT]"]
  L1 = Inductor [inductance=10µH package="400 mil [THT]"]
  IC1 = IC, DIP package, 22 pins [chip_label=AD9850]
  IC2 = MICROCONTROLLER [package=dil28-3-simon]
  VCC1 = Battery
  S1 = SWITCH-MOMENTARY-2 [package=tactile_switch_smd-2]
  S2 = SWITCH-MOMENTARY-2 [package=tactile_switch_smd-2]
  S3 = SWITCH-MOMENTARY-2 [package=tactile_switch_smd-2]
  S4 = SWITCH-MOMENTARY-2 [package=tactile_switch_smd-2]
  ANT1 = Antenna
  IC3 = Voltage Regulator [package=to-220-alt]
  D1 = Diode [package=diode-1n4001]
  C2 = Ceramic Capacitor [capacitance=10nF package="0603 [SMD, multilayer]"]
  C3 = Ceramic Capacitor [capacitance=47µF package="0603 [SMD, multilayer]"]
  C4 = Ceramic Capacitor [capacitance=1nF package="100 mil [THT, multilayer]"]

nets:
  VSS: LCD1.VSS, LCD1.V0, LCD1.R/W, Q1.E, IC1.pin7, IC1.pin12, VCC1.-, S1.2, S2.2, S3.2, S4.2, IC3.GND, C2.0, C3.0, C4.0
  N1: LCD1.VDD, IC1.pin1, IC1.pin22, IC2.PC6(_RESET), IC2.AVCC, IC2.AREF, VCC1.+, IC3.OUT, C2.1, C3.1
  N2: LCD1.RS, IC2.PC1(ADC1)
  N3: LCD1.E, IC2.PC0(ADC0)
  N4: LCD1.DB4, IC2.PD4(XCK_T0)
  N5: LCD1.DB5, IC2.PD5(T1)
  N6: LCD1.DB6, IC2.PD6(AIN0)
  N7: LCD1.DB7, IC2.PD7(AIN1)
  N8: R1.Pin_0, L1.pin_0, D1.A
  N9: R1.Pin_1, Q1.B
  N10: Q1.C, L1.pin_1, ANT1.antenna_lead
  N11: IC1.pin2, IC2.PB0(ICP)
  N12: IC1.pin3, IC2.PB1(OC1A)
  N13: IC1.pin4, IC2.PB2(SS_OC1B)
  N14: IC1.pin5, IC2.PB3(MOSI_OC2)
  N15: IC2.PD0(RXD), S1.1
  N16: IC2.PD1(TXD), S2.1
  N17: IC2.PD2(INT0), S3.1
  N18: IC2.PD3(INT1), S4.1
  N19: IC3.IN, D1.C
